# Fritzing sketch 2.AccelBasic (saved by Fritzing 0.9.3b)
breadboards: 1

parts:
  Part1 = Arduino Nano (Rev3.0)
  IC1 = DIP - 10 pins [chip_label=ADXL345 package="DIP (Dual Inline) [THT]"]

nets:
  GND: Part1.GND, IC1.GND
  5V: Part1.5V, IC1.5V
  N1: Part1.A5, IC1.SCL
  N2: Part1.A4, IC1.SDA

custom parts:
  DIP - 10 pins: A DIP stand-in part for whatever IC you want. With 10 pins on a 900mil dual inline package (DIP) footprint.
