# Fritzing sketch 3.Ultrasound (saved by Fritzing 0.9.3b)
breadboards: 1

parts:
  Part1 = Arduino Nano (Rev3.0)
  Part2 = Breakout Board for Electret Microphone
  Part3 = SRF05 Ultrasonic Rangefinder

nets:
  GND: Part1.GND, Part2.AUD, Part3.GND
  N1: Part1.D2, Part3.Trig
  N2: Part1.D3, Part3.Echo
  N3: Part1.D8, Part2.VCC
  5V: Part1.5V, Part3.VCC
